// Logisim project jdh8.circ as structural Verilog: 10 circuits, main circuit main
module main (
);

  wire addr_1_eaux, addr_1_eramout, addr_1_erom, addr_1_lramout, aimm, and_1_out, and_2_out, asp, cc, clk,
       clock_1_out, ealu, edev, eop1, eop2, eram, ereg, err, ex, fall, hlt, jnz, ldev, ldf, ldh, ldl, ldx,
       ldy, lop, lprt, lram, lreg, not_1_out, not_2_out, not_3_out, not_4_out, not_5_out, not_6_out,
       not_7_out, pow, rise, sel, spdec, spinc;
  wire [2:0] addr_1_selaux, exc, sel0, sel1;
  wire [3:0] op;
  wire [7:0] dbus, f, op0, op1, op2, ram_1_dout, regs_1_hout, regs_1_lout, rom_1_data;
  wire [15:0] addr_1_addrout, auxregs_1_pcout, auxregs_1_spout;

  and and_1 (and_1_out, eram, addr_1_eaux);
  and and_2 (and_2_out, lram, addr_1_eaux);
  regs regs_1 (
    .lout(regs_1_lout), .fout(f), .dout(dbus), .hout(regs_1_hout), .ereg(ereg), .sel(sel), .ldh(ldh),
    .ldl(ldl), .ldf(ldf), .sel0(sel0), .sel1(sel1), .din(dbus), .clk(clk), .lreg(lreg));
  auxregs auxregs_1 (
    .pcout(auxregs_1_pcout), .spout(auxregs_1_spout), .dbusout(dbus), .clk(clk), .sel(addr_1_selaux),
    .h(regs_1_hout), .l(regs_1_lout), .dbus(dbus), .lop(lop), .jnz(jnz), .en(and_1_out), .ld(and_2_out),
    .spinc(spinc), .spdec(spdec));
  alu alu_1 (.dout(dbus), .op(op[2:0]), .clk(clk), .ldx(ldx), .ldy(ldy), .ealu(ealu), .ldf(ldf), .fin(f), .din(dbus));
  Clock clock_1 (.out(clock_1_out));
  and and_3 (clk, clock_1_out, not_1_out);
  not not_1 (not_1_out, hlt);
  not not_2 (not_2_out, clk);
  not not_3 (not_3_out, clk);
  not not_4 (not_4_out, not_3_out);
  not not_5 (not_5_out, clk);
  not not_6 (not_6_out, not_5_out);
  not not_7 (not_7_out, not_6_out);
  and and_4 (fall, not_2_out, not_4_out);
  and and_5 (rise, clk, not_7_out);
  addr addr_1 (
    .eramout(addr_1_eramout), .lramout(addr_1_lramout), .eaux(addr_1_eaux), .selaux(addr_1_selaux),
    .addrout(addr_1_addrout), .erom(addr_1_erom), .eram(eram), .apc(lop), .asp(asp), .aimm(aimm),
    .hl({regs_1_hout, regs_1_lout}), .pc(auxregs_1_pcout), .sp(auxregs_1_spout), .imm({op2, op1}), .lram(lram));
  dev dev_1 (
    .dbusout(dbus), .powout(pow), .hltout(hlt), .errout(err), .clk(clk), .edev(edev), .ldev(ldev),
    .lprt(lprt), .dbusin(dbus));
  ROM #(.addrWidth(15)) rom_1 (.addr(addr_1_addrout[14:0]), .data(rom_1_data));
  RAM #(.addrWidth(15), .clearpin("true"), .enables("line")) ram_1 (
    .addr(addr_1_addrout[14:0]), .we(addr_1_lramout), .clk(clk), .din(dbus), .dout(ram_1_dout), .clr(1'b0));
  opc opc_1 (
    .sel0(sel0), .sel1(sel1), .lop(lop), .ex(ex), .excout(exc), .op1out(op1), .op2out(op2), .dbusout(dbus),
    .op0out(op0), .op(op), .dbus(dbus), .fall(fall), .cc(cc), .eop1(eop1), .eop2(eop2), .clk(clk));
  assign dbus = addr_1_erom ? rom_1_data : 8'bz;  // Controlled_Buffer controlled_buffer_1
  assign dbus = addr_1_eramout ? ram_1_dout : 8'bz;  // Controlled_Buffer controlled_buffer_2
  control control_1 (
    .ldy(ldy), .ldf(ldf), .ealu(ealu), .ldh(ldh), .ldl(ldl), .lprt(lprt), .ldev(ldev), .ldx(ldx), .cc(cc),
    .ereg(ereg), .lreg(lreg), .sel(sel), .asp(asp), .aimm(aimm), .lram(lram), .spinc(spinc), .spdec(spdec),
    .jnz(jnz), .eram(eram), .eop1(eop1), .eop2(eop2), .edev(edev), .op0(op0), .ex(ex), .exc(exc));

  // Notes on the sheet:
  //   contents of rom_1 (hex, n*v repeats v):
  //   50 ff fe 24 fc ff 25 fd ff 30 6 48 30 1 30 2 49 4a 30 3 30 4 30 5 4b 77 0 c7 8 87
endmodule

module opc (
  input  clk,
  input  [7:0] dbus,
  input  fall,
  input  cc,
  input  eop1,
  input  eop2,
  output [7:0] op0out,
  output [3:0] op,
  output [2:0] sel0,
  output [2:0] sel1,
  output lop,
  output ex,
  output [2:0] excout,
  output [7:0] op1out,
  output [7:0] op2out,
  output [7:0] dbusout
);

  wire and_1_out, and_2_out, and_3_out, and_4_out, and_5_out, and_6_out, and_7_out, and_8_out, and_10_out,
       and_11_out, and_13_out, and_14_out, and_15_out, and_16_out, comparator_1_lt, decoder_1_out0,
       decoder_1_out1, decoder_1_out2, decoder_1_out3, ld1, ld2, ld3, nand_1_out, not_1_out, not_2_out,
       not_3_out, not_4_out, not_5_out, or_1_out, or_2_out, or_3_out, or_4_out;
  wire [7:0] opc_q;
  wire [7:3] exc_q;

  and and_1 (and_1_out, cc, fall);
  Comparator #(.mode("unsigned"), .width(4)) comparator_1 (.a(op), .b(4'b0111), .lt(comparator_1_lt));  // open: gt, eq
  not not_1 (not_1_out, op[0]);
  not not_2 (not_2_out, op[1]);
  not not_3 (not_3_out, op[2]);
  and and_2 (and_2_out, op[0], not_3_out, not_2_out);
  not not_4 (not_4_out, op0out[3]);
  and and_3 (and_3_out, not_4_out, or_1_out);
  and and_4 (and_4_out, lop, decoder_1_out0);
  and and_5 (and_5_out, lop, decoder_1_out1);
  and and_6 (and_6_out, lop, decoder_1_out2);
  and and_7 (and_7_out, not_1_out, op[1], not_1_out);
  and and_8 (and_8_out, op[0], not_2_out, op[2]);
  or or_1 (or_1_out, and_2_out, and_7_out);
  or or_2 (or_2_out, and_3_out, and_8_out);
  and and_9 (ld3, comparator_1_lt, or_2_out);
  nor nor_1 (ld2, ld3, ld1);
  Register op0 (.D(dbus), .en(and_4_out), .clk(clk), .Q({op, op0out[3:0]}), .clr(1'b0));
  Register op1 (.D(dbus), .en(and_5_out), .clk(clk), .Q(op1out), .clr(1'b0));
  Register op2 (.D(dbus), .en(and_6_out), .clk(clk), .Q(op2out), .clr(1'b0));
  Counter #(.trigger("falling")) opc (
    .count(lop), .Q(opc_q), .up(1'b1), .clk(clk), .clr(and_1_out));  // open: load, D, carry
  Counter #(.trigger("falling")) exc (
    .count(ex), .Q({exc_q, excout}), .up(1'b1), .clk(clk), .clr(and_1_out));  // open: load, D, carry
  and and_10 (and_10_out, op[2], not_2_out, not_1_out);
  or or_3 (or_3_out, and_10_out, op0out[3]);
  and and_11 (and_11_out, or_3_out, and_13_out);
  not not_5 (not_5_out, and_8_out);
  and and_12 (ld1, not_5_out, and_11_out);
  Decoder #(.select(2)) decoder_1 (
    .out0(decoder_1_out0), .out1(decoder_1_out1), .out2(decoder_1_out2), .out3(decoder_1_out3),
    .sel(opc_q[1:0]), .en(1'b1));
  nand nand_1 (nand_1_out, not_3_out, not_2_out, not_1_out);
  and and_13 (and_13_out, comparator_1_lt, nand_1_out);
  assign dbusout = eop1 ? op1out : 8'bz;  // Controlled_Buffer controlled_buffer_1
  assign dbusout = eop2 ? op2out : 8'bz;  // Controlled_Buffer controlled_buffer_2
  and and_14 (and_14_out, decoder_1_out1, ld1);
  or or_4 (or_4_out, and_14_out, and_15_out);
  or or_5 (ex, or_4_out, and_16_out);
  and and_15 (and_15_out, decoder_1_out2, ld2);
  and and_16 (and_16_out, decoder_1_out3, ld3);
  not not_6 (lop, ex);

  assign op0out[7:4] = op;
  assign sel0 = op0out[2:0];
  assign sel1 = op1out[2:0];

  // Other names for the same wires on the sheet: exc[2:0] = excout; y = op0out[3]
endmodule

module auxregs (
  input  clk,
  input  [2:0] sel,
  input  [7:0] h,
  input  [7:0] l,
  input  [7:0] dbus,
  input  lop,
  input  jnz,
  input  en,
  input  ld,
  input  spinc,
  input  spdec,
  output [15:0] pcout,
  output [15:0] spout,
  output [7:0] dbusout
);

  wire and_1_out, and_2_out, and_3_out, and_4_out, and_5_out, and_6_out, and_7_out, and_8_out, and_9_out,
       and_10_out, and_11_out, and_12_out, and_13_out, comparator_1_gt, comparator_1_lt, decoder_1_out2,
       decoder_1_out3, decoder_1_out4, decoder_1_out5, decoder_1_out6, decoder_1_out7, not_1_out, not_2_out,
       or_1_out, or_2_out, or_3_out, or_4_out, or_5_out, or_6_out, or_7_out;
  wire [7:0] controlled_buffer_1_out, controlled_buffer_2_out, controlled_buffer_3_out,
       controlled_buffer_4_out, mbl_q;
  wire [15:0] adder_1_out, multiplexer_1_out, multiplexer_2_out;

  Multiplexer #(.enable("false"), .width(16)) multiplexer_1 (
    .in0(pcout), .in1(spout), .out(multiplexer_1_out), .sel(or_1_out));
  or or_1 (or_1_out, spinc, spdec);
  Multiplexer #(.enable("false"), .width(16)) multiplexer_2 (
    .in0(16'h1), .in1({16{1'b1}}), .out(multiplexer_2_out), .sel(spdec));
  Adder #(.width(16)) adder_1 (
    .a(multiplexer_1_out), .b(multiplexer_2_out), .out(adder_1_out), .cin(1'b0));  // open: cout
  or or_2 (or_2_out, lop, and_1_out);
  not not_1 (not_1_out, or_2_out);
  not not_2 (not_2_out, or_1_out);
  or or_3 (or_3_out, comparator_1_gt, comparator_1_lt);
  Comparator comparator_1 (.a({8{1'b0}}), .b(dbus), .gt(comparator_1_gt), .lt(comparator_1_lt));  // open: eq
  assign controlled_buffer_1_out = not_1_out ? dbus : 8'bz;  // Controlled_Buffer controlled_buffer_1
  assign controlled_buffer_2_out = not_1_out ? dbus : 8'bz;  // Controlled_Buffer controlled_buffer_2
  assign controlled_buffer_3_out = not_2_out ? dbus : 8'bz;  // Controlled_Buffer controlled_buffer_3
  assign controlled_buffer_4_out = not_2_out ? dbus : 8'bz;  // Controlled_Buffer controlled_buffer_4
  and and_1 (and_1_out, jnz, or_3_out);
  assign controlled_buffer_1_out = lop ? adder_1_out[7:0] : 8'bz;  // Controlled_Buffer controlled_buffer_5
  assign controlled_buffer_1_out = and_1_out ? l : 8'bz;  // Controlled_Buffer controlled_buffer_6
  assign controlled_buffer_2_out = lop ? adder_1_out[15:8] : 8'bz;  // Controlled_Buffer controlled_buffer_7
  assign controlled_buffer_2_out = and_1_out ? h : 8'bz;  // Controlled_Buffer controlled_buffer_8
  assign controlled_buffer_3_out = or_1_out ? adder_1_out[7:0] : 8'bz;  // Controlled_Buffer controlled_buffer_9
  assign controlled_buffer_4_out = or_1_out ? adder_1_out[15:8] : 8'bz;  // Controlled_Buffer controlled_buffer_10
  Register pcl (.D(controlled_buffer_1_out), .en(or_4_out), .clk(clk), .Q(pcout[7:0]));  // open: clr
  or or_4 (or_4_out, or_2_out, and_2_out);
  Register pch (.D(controlled_buffer_2_out), .en(or_5_out), .clk(clk), .Q(pcout[15:8]));  // open: clr
  or or_5 (or_5_out, or_2_out, and_3_out);
  Register spl (.D(controlled_buffer_3_out), .en(or_6_out), .clk(clk), .Q(spout[7:0]));  // open: clr
  or or_6 (or_6_out, or_1_out, and_4_out);
  Register sph (.D(controlled_buffer_4_out), .en(or_7_out), .clk(clk), .Q(spout[15:8]));  // open: clr
  or or_7 (or_7_out, or_1_out, and_5_out);
  Register mbl (.D(dbus), .en(and_6_out), .clk(clk), .Q(mbl_q));  // open: clr
  Register mbh (.D(dbus), .en(and_7_out), .clk(clk), .Q(mbl_q));  // open: clr
  and and_2 (and_2_out, ld, decoder_1_out6);
  and and_3 (and_3_out, ld, decoder_1_out7);
  and and_4 (and_4_out, ld, decoder_1_out4);
  and and_5 (and_5_out, ld, decoder_1_out5);
  and and_6 (and_6_out, ld, decoder_1_out2);
  and and_7 (and_7_out, ld, decoder_1_out3);
  Decoder #(.select(3)) decoder_1 (
    .out2(decoder_1_out2), .out3(decoder_1_out3), .out4(decoder_1_out4), .out5(decoder_1_out5),
    .out6(decoder_1_out6), .out7(decoder_1_out7), .sel(sel), .en(1'b1));  // open: out0, out1
  assign dbusout = and_8_out ? pcout[7:0] : 8'bz;  // Controlled_Buffer controlled_buffer_11
  and and_8 (and_8_out, decoder_1_out6, en);
  assign dbusout = and_9_out ? pcout[15:8] : 8'bz;  // Controlled_Buffer controlled_buffer_12
  and and_9 (and_9_out, decoder_1_out7, en);
  assign dbusout = and_10_out ? spout[7:0] : 8'bz;  // Controlled_Buffer controlled_buffer_13
  and and_10 (and_10_out, decoder_1_out4, en);
  assign dbusout = and_11_out ? spout[15:8] : 8'bz;  // Controlled_Buffer controlled_buffer_14
  and and_11 (and_11_out, decoder_1_out5, en);
  assign dbusout = and_12_out ? mbl_q : 8'bz;  // Controlled_Buffer controlled_buffer_15
  and and_12 (and_12_out, decoder_1_out2, en);
  assign dbusout = and_13_out ? mbl_q : 8'bz;  // Controlled_Buffer controlled_buffer_16
  and and_13 (and_13_out, decoder_1_out3, en);

  // Other names for the same wires on the sheet: pc[15:0] = pcout; sp[15:0] = spout
endmodule

module addr (
  input  lram,
  input  eram,
  input  apc,
  input  asp,
  input  aimm,
  input  [15:0] hl,
  input  [15:0] pc,
  input  [15:0] sp,
  input  [15:0] imm,
  output erom,
  output eramout,
  output lramout,
  output eaux,
  output [2:0] selaux,
  output [15:0] addrout
);

  wire and_2_out, and_3_out, nor_1_out, not_1_out, not_2_out, or_1_out, or_2_out;

  or or_1 (or_1_out, eram, apc);
  nor nor_1 (nor_1_out, apc, asp, aimm);
  assign addrout = nor_1_out ? hl : 16'bz;  // Controlled_Buffer controlled_buffer_1
  assign addrout = apc ? pc : 16'bz;  // Controlled_Buffer controlled_buffer_2
  assign addrout = asp ? sp : 16'bz;  // Controlled_Buffer controlled_buffer_3
  assign addrout = aimm ? imm : 16'bz;  // Controlled_Buffer controlled_buffer_4
  or or_2 (or_2_out, addrout[1], addrout[2]);
  and and_1 (eaux, or_2_out, and_2_out);
  and and_2 (and_2_out, addrout[3], addrout[4], addrout[5], addrout[6], addrout[7], addrout[8], addrout[9], addrout[10], addrout[11], addrout[12], addrout[13], addrout[14], addrout[15]);
  and and_3 (and_3_out, addrout[15], not_1_out);
  not not_1 (not_1_out, eaux);
  Hex_Digit_Display hex_digit_display_1 (.value(addrout[15:12]));  // open: dp
  and and_4 (erom, or_1_out, not_2_out);
  not not_2 (not_2_out, addrout[15]);
  and and_5 (eramout, or_1_out, and_3_out);
  and and_6 (lramout, and_3_out, lram);
  Hex_Digit_Display hex_digit_display_2 (.value(addrout[11:8]));  // open: dp
  Hex_Digit_Display hex_digit_display_3 (.value(addrout[7:4]));  // open: dp
  Hex_Digit_Display hex_digit_display_4 (.value(addrout[3:0]));  // open: dp

  assign selaux = addrout[2:0];
endmodule

module dev (
  input  clk,
  input  edev,
  input  ldev,
  input  lprt,
  input  [7:0] dbusin,
  output errout,
  output powout,
  output hltout,
  output [7:0] dbusout
);

  wire and_1_out, and_2_out, nand_1_out;
  wire [7:0] prt_q, sta_q;

  nand nand_1 (nand_1_out, prt_q[7], prt_q[6], prt_q[5], prt_q[4], prt_q[3], prt_q[2], prt_q[1], prt_q[0]);
  and and_1 (and_1_out, edev, nand_1_out);
  and and_2 (and_2_out, ldev, nand_1_out);
  Register sta (
    .D(dbusin), .en(and_2_out), .clk(clk), .Q({sta_q[7:4], hltout, powout, errout, sta_q[0]}));  // open: clr
  Register prt (.D(dbusin), .en(lprt), .clk(clk), .Q(prt_q));  // open: clr
  LED err (.in(errout));
  LED pow (.in(powout));
  assign dbusout = and_1_out ? {sta_q[7:4], hltout, powout, errout, sta_q[0]} : 8'bz;  // Controlled_Buffer controlled_buffer_1
  LED hlt (.in(hltout));
endmodule

module regs (
  input  lreg,
  input  ereg,
  input  sel,
  input  ldh,
  input  ldl,
  input  ldf,
  input  [2:0] sel0,
  input  [2:0] sel1,
  input  [7:0] din,
  input  clk,
  output [7:0] dout,
  output [7:0] lout,
  output [7:0] hout,
  output [7:0] fout
);

  wire and_1_out, and_2_out, decoder_1_out0, decoder_1_out1, decoder_1_out2, decoder_1_out3, decoder_1_out4,
       decoder_1_out5, decoder_1_out6, decoder_1_out7, decoder_2_out0, decoder_2_out1, decoder_2_out2,
       decoder_2_out3, decoder_2_out4, decoder_2_out5, decoder_2_out6, decoder_2_out7, not_1_out, not_2_out,
       or_1_out, or_2_out, or_3_out;
  wire [2:0] controlled_buffer_1_out;
  wire [7:0] A_q, B_q, C_q, D_q, Z_q;

  not not_1 (not_1_out, or_1_out);
  not not_2 (not_2_out, sel);
  or or_1 (or_1_out, ldf, or_2_out);
  and and_1 (and_1_out, not_1_out, not_2_out);
  and and_2 (and_2_out, sel, not_1_out);
  or or_2 (or_2_out, ldl, ldh);
  assign controlled_buffer_1_out = and_1_out ? sel0 : 3'bz;  // Controlled_Buffer controlled_buffer_1
  assign controlled_buffer_1_out = and_2_out ? sel1 : 3'bz;  // Controlled_Buffer controlled_buffer_2
  assign controlled_buffer_1_out = ldh ? 3'b101 : 3'bz;  // Controlled_Buffer controlled_buffer_3
  assign controlled_buffer_1_out = ldl ? 3'b100 : 3'bz;  // Controlled_Buffer controlled_buffer_4
  assign controlled_buffer_1_out = ldf ? 3'b111 : 3'bz;  // Controlled_Buffer controlled_buffer_5
  or or_3 (or_3_out, lreg, or_1_out);
  Decoder #(.select(3)) decoder_1 (
    .out0(decoder_1_out0), .out1(decoder_1_out1), .out2(decoder_1_out2), .out3(decoder_1_out3),
    .out4(decoder_1_out4), .out5(decoder_1_out5), .out6(decoder_1_out6), .out7(decoder_1_out7),
    .sel(controlled_buffer_1_out), .en(or_3_out));
  Register A (.D(din), .en(decoder_1_out0), .clk(clk), .Q(A_q), .clr(1'b0));
  Register B (.D(din), .en(decoder_1_out1), .clk(clk), .Q(B_q), .clr(1'b0));
  Register C (.D(din), .en(decoder_1_out2), .clk(clk), .Q(C_q), .clr(1'b0));
  Register D (.D(din), .en(decoder_1_out3), .clk(clk), .Q(D_q), .clr(1'b0));
  Register L (.D(din), .en(decoder_1_out4), .clk(clk), .Q(lout), .clr(1'b0));
  Register H (.D(din), .en(decoder_1_out5), .clk(clk), .Q(hout), .clr(1'b0));
  Register Z (.D(din), .en(decoder_1_out6), .clk(clk), .Q(Z_q), .clr(1'b0));
  Register F (.D(din), .en(decoder_1_out7), .clk(clk), .Q(fout), .clr(1'b0));
  Decoder #(.select(3)) decoder_2 (
    .out0(decoder_2_out0), .out1(decoder_2_out1), .out2(decoder_2_out2), .out3(decoder_2_out3),
    .out4(decoder_2_out4), .out5(decoder_2_out5), .out6(decoder_2_out6), .out7(decoder_2_out7),
    .sel(controlled_buffer_1_out), .en(ereg));
  assign dout = decoder_2_out0 ? A_q : 8'bz;  // Controlled_Buffer controlled_buffer_6
  assign dout = decoder_2_out1 ? B_q : 8'bz;  // Controlled_Buffer controlled_buffer_7
  assign dout = decoder_2_out2 ? C_q : 8'bz;  // Controlled_Buffer controlled_buffer_8
  assign dout = decoder_2_out3 ? D_q : 8'bz;  // Controlled_Buffer controlled_buffer_9
  assign dout = decoder_2_out4 ? lout : 8'bz;  // Controlled_Buffer controlled_buffer_10
  assign dout = decoder_2_out5 ? hout : 8'bz;  // Controlled_Buffer controlled_buffer_11
  assign dout = decoder_2_out6 ? Z_q : 8'bz;  // Controlled_Buffer controlled_buffer_12
  assign dout = decoder_2_out7 ? fout : 8'bz;  // Controlled_Buffer controlled_buffer_13
endmodule

module control (
  input  ex,
  input  [2:0] exc,
  input  [7:0] op0,
  output eram,
  output ldx,
  output asp,
  output ldy,
  output aimm,
  output ldf,
  output lram,
  output ealu,
  output spinc,
  output ldh,
  output spdec,
  output ldl,
  output jnz,
  output lprt,
  output ereg,
  output lreg,
  output sel,
  output eop1,
  output eop2,
  output edev,
  output ldev,
  output cc
);

  wire and_1_out, and_13_out, not_1_out;
  wire [3:0] rom_1_data, rom_1_data_2, rom_1_data_3, rom_1_data_4;

  Hex_Digit_Display hex_digit_display_1 (.value(rom_1_data_4));  // open: dp
  ROM #(.addrWidth(12), .dataWidth(16)) rom_1 (
    .addr({4'b0000, op0[7:3], exc}), .data({rom_1_data_4, rom_1_data_3, rom_1_data_2, rom_1_data}));
  Hex_Digit_Display hex_digit_display_2 (.value(rom_1_data_3));  // open: dp
  Hex_Digit_Display hex_digit_display_3 (.value(rom_1_data_2));  // open: dp
  Hex_Digit_Display hex_digit_display_4 (.value(rom_1_data));  // open: dp
  and and_1 (and_1_out, not_1_out, ex);
  not not_1 (not_1_out, rom_1_data_4[3]);
  and and_2 (ereg, rom_1_data_2[3], ex);
  and and_3 (eram, rom_1_data[0], and_1_out);
  and and_4 (asp, rom_1_data[1], and_1_out);
  and and_5 (aimm, rom_1_data[2], and_1_out);
  and and_6 (lram, rom_1_data[3], and_1_out);
  and and_7 (spinc, rom_1_data_2[0], and_1_out);
  and and_8 (spdec, rom_1_data_2[1], and_1_out);
  and and_9 (jnz, rom_1_data_2[2], and_1_out);
  and and_10 (lreg, rom_1_data_3[0], ex);
  and and_11 (sel, rom_1_data_3[1], ex);
  and and_12 (eop1, rom_1_data_3[2], ex);
  and and_13 (and_13_out, rom_1_data_4[3], ex);
  and and_14 (eop2, rom_1_data_3[3], ex);
  and and_15 (edev, rom_1_data_4[0], ex);
  and and_16 (ldx, rom_1_data[0], and_13_out);
  and and_17 (ldy, rom_1_data[1], and_13_out);
  and and_18 (ldf, rom_1_data[2], and_13_out);
  and and_19 (ealu, rom_1_data[3], and_13_out);
  and and_20 (ldh, rom_1_data_2[0], and_13_out);
  and and_21 (ldl, rom_1_data_2[1], and_13_out);
  and and_22 (lprt, rom_1_data_2[2], and_13_out);
  and and_23 (ldev, rom_1_data_4[1], ex);
  and and_24 (cc, rom_1_data_4[2], ex);

  // Notes on the sheet:
  //   contents of rom_1 (hex, n*v repeats v):
  //   4500 7*4000 8281 c108 6*4000 4105 7*4000 4101 7*4000 408c 7*4000 4088 7*4000 40a 4020 6*4000 8a 4020
  //   14*4000 10 4103 6*4000 8420 c810 14*4000 4440 7*4000 40c0 7*4000 8440 5100 6*4000 82c0 5100 6*4000
  //   8440 6080 6*4000 82c0 6080 6*4000 8081 8402 8108 c004 4*4000 8081 8282 8108 c004 4*4000 8081 8402
  //   8108 c004 4*4000 8081 8282 8108 c004 4*4000 8081 8402 c108 5*4000 8081 8282 c108 5*4000 8081 8402
  //   c108 5*4000 8081 8282 c108 5*4000 8081 8402 c108 5*4000 8081 8282 c108 5*4000 8081 8402 c004 5*4000
  //   8081 8282 c004 5*4000 8081 8402 8108 c004 4*4000 8081 8282 8108 c004 4*4000
endmodule

module alu (
  input  [2:0] op,
  input  clk,
  input  ldx,
  input  ldy,
  input  ealu,
  input  ldf,
  input  [7:0] din,
  input  [7:0] fin,
  output [7:0] dout
);

  wire adder_1_cout, and_1_out, and_3_out, and_4_out, decoder_1_out0, decoder_1_out1, decoder_1_out2,
       decoder_1_out3, decoder_1_out4, decoder_1_out5, decoder_1_out7, or_1_out, subtractor_1_bout;
  wire [3:0] comparator_1_lt;
  wire [7:0] adder_1_out, and_2_out, controlled_buffer_1_out, nor_1_out, or_2_out, register_1_q,
       register_2_q, subtractor_1_out;

  Register register_1 (.D(din), .en(ldx), .clk(clk), .Q(register_1_q));  // open: clr
  Register register_2 (.D(din), .en(ldy), .clk(clk), .Q(register_2_q));  // open: clr
  Decoder #(.select(3)) decoder_1 (
    .out0(decoder_1_out0), .out1(decoder_1_out1), .out2(decoder_1_out2), .out3(decoder_1_out3),
    .out4(decoder_1_out4), .out5(decoder_1_out5), .out7(decoder_1_out7), .sel(op), .en(1'b1));  // open: out6
  and and_1 (and_1_out, fin[2], op[1]);
  Adder adder_1 (.a(register_1_q), .b(register_2_q), .out(adder_1_out), .cin(and_1_out), .cout(adder_1_cout));
  or or_1 (or_1_out, decoder_1_out1, decoder_1_out2);
  assign and_2_out = register_1_q & register_2_q;  // AND_Gate and_2, 8 bits wide
  assign or_2_out = register_1_q | register_2_q;  // OR_Gate or_2, 8 bits wide
  assign nor_1_out = ~(register_1_q | register_2_q);  // NOR_Gate nor_1, 8 bits wide
  Comparator comparator_1 (
    .a(register_1_q), .b(register_2_q), .eq(comparator_1_lt[1]), .lt(comparator_1_lt[0]));  // open: gt
  Subtractor subtractor_1 (
    .a(register_1_q), .b(register_2_q), .out(subtractor_1_out), .bin(fin[3]), .bout(subtractor_1_bout));
  and and_3 (and_3_out, decoder_1_out7, subtractor_1_bout);
  assign controlled_buffer_1_out = or_1_out ? adder_1_out : 8'bz;  // Controlled_Buffer controlled_buffer_1
  and and_4 (and_4_out, adder_1_cout, or_1_out);
  assign controlled_buffer_1_out = decoder_1_out3 ? and_2_out : 8'bz;  // Controlled_Buffer controlled_buffer_2
  assign controlled_buffer_1_out = decoder_1_out4 ? or_2_out : 8'bz;  // Controlled_Buffer controlled_buffer_3
  assign controlled_buffer_1_out = decoder_1_out5 ? nor_1_out : 8'bz;  // Controlled_Buffer controlled_buffer_4
  assign controlled_buffer_1_out = decoder_1_out7 ? subtractor_1_out : 8'bz;  // Controlled_Buffer controlled_buffer_5
  or or_3 (comparator_1_lt[3], and_3_out, fin[3]);
  assign controlled_buffer_1_out = decoder_1_out0 ? register_1_q : 8'bz;  // Controlled_Buffer controlled_buffer_6
  or or_4 (comparator_1_lt[2], fin[2], and_4_out);
  assign dout = ealu ? controlled_buffer_1_out : 8'bz;  // Controlled_Buffer controlled_buffer_7
  assign dout = ldf ? {4'b0000, comparator_1_lt} : 8'bz;  // Controlled_Buffer controlled_buffer_8
  RAM #(.addrWidth(15), .clearpin("true"), .enables("line")) ram_1 ();  // open: addr, we, clk, din, dout, clr
  RAM #(.addrWidth(15), .clearpin("true"), .enables("line")) ram_2 ();  // open: addr, we, clk, din, dout, clr

  // Other names for the same wires on the sheet: fl = fin[0]; fe = fin[1]; fc = fin[2]; fb = fin[3]
endmodule

module main2 (
);

  wire addr_1_eaux, addr_1_eramout, addr_1_erom, addr_1_lramout, and_1_out, and_2_out, and_3_out, and_4_out,
       clock_1_out, control_1_aimm, control_1_asp, control_1_cc, control_1_ealu, control_1_edev,
       control_1_eop1, control_1_eop2, control_1_eram, control_1_ereg, control_1_jnz, control_1_ldev,
       control_1_ldf, control_1_ldh, control_1_ldl, control_1_ldx, control_1_ldy, control_1_lprt,
       control_1_lram, control_1_lreg, control_1_sel, control_1_spdec, control_1_spinc, dev_1_hltout,
       not_1_out, not_2_out, not_3_out, not_4_out, opc_1_ex, opc_1_lop;
  wire [2:0] addr_1_selaux, opc_1_excout, opc_1_sel0, opc_1_sel1;
  wire [3:0] opc_1_op;
  wire [7:0] auxregs_1_dbusout, opc_1_op0out, opc_1_op1out, opc_1_op2out, ram_1_dout, regs_1_fout,
       regs_1_hout, regs_1_lout, rom_1_data;
  wire [15:0] addr_1_addrout, auxregs_1_pcout, auxregs_1_spout;

  Clock clock_1 (.out(clock_1_out));
  not not_1 (not_1_out, dev_1_hltout);
  and and_1 (and_1_out, addr_1_eaux, control_1_eram);
  and and_2 (and_2_out, addr_1_eaux, control_1_lram);
  not not_2 (not_2_out, and_3_out);
  not not_3 (not_3_out, and_3_out);
  not not_4 (not_4_out, not_3_out);
  and and_3 (and_3_out, clock_1_out, not_1_out);
  and and_4 (and_4_out, not_2_out, not_4_out);
  control control_1 (
    .ldy(control_1_ldy), .ldf(control_1_ldf), .ealu(control_1_ealu), .ldh(control_1_ldh),
    .ldl(control_1_ldl), .lprt(control_1_lprt), .ldev(control_1_ldev), .ldx(control_1_ldx),
    .cc(control_1_cc), .ereg(control_1_ereg), .lreg(control_1_lreg), .sel(control_1_sel),
    .asp(control_1_asp), .aimm(control_1_aimm), .lram(control_1_lram), .spinc(control_1_spinc),
    .spdec(control_1_spdec), .jnz(control_1_jnz), .eram(control_1_eram), .eop1(control_1_eop1),
    .eop2(control_1_eop2), .edev(control_1_edev), .op0(opc_1_op0out), .ex(opc_1_ex), .exc(opc_1_excout));
  auxregs auxregs_1 (
    .pcout(auxregs_1_pcout), .spout(auxregs_1_spout), .dbusout(auxregs_1_dbusout), .clk(and_3_out),
    .sel(addr_1_selaux), .h(regs_1_hout), .l(regs_1_lout), .dbus(auxregs_1_dbusout), .lop(opc_1_lop),
    .jnz(control_1_jnz), .en(and_1_out), .ld(and_2_out), .spinc(control_1_spinc), .spdec(control_1_spdec));
  LED led_1 (.in(auxregs_1_dbusout[7]));
  LED led_2 (.in(auxregs_1_dbusout[6]));
  LED led_3 (.in(auxregs_1_dbusout[5]));
  LED led_4 (.in(auxregs_1_dbusout[4]));
  LED led_5 (.in(auxregs_1_dbusout[3]));
  LED led_6 (.in(auxregs_1_dbusout[0]));
  LED led_7 (.in(auxregs_1_dbusout[2]));
  LED led_8 (.in(auxregs_1_dbusout[1]));
  addr addr_1 (
    .eramout(addr_1_eramout), .lramout(addr_1_lramout), .eaux(addr_1_eaux), .selaux(addr_1_selaux),
    .addrout(addr_1_addrout), .erom(addr_1_erom), .eram(control_1_eram), .apc(opc_1_lop),
    .asp(control_1_asp), .aimm(control_1_aimm), .hl({regs_1_hout, regs_1_lout}), .pc(auxregs_1_pcout),
    .sp(auxregs_1_spout), .imm({opc_1_op2out, opc_1_op1out}), .lram(control_1_lram));
  regs regs_1 (
    .lout(regs_1_lout), .fout(regs_1_fout), .dout(auxregs_1_dbusout), .hout(regs_1_hout),
    .ereg(control_1_ereg), .sel(control_1_sel), .ldh(control_1_ldh), .ldl(control_1_ldl),
    .ldf(control_1_ldf), .sel0(opc_1_sel0), .sel1(opc_1_sel1), .din(auxregs_1_dbusout), .clk(and_3_out),
    .lreg(control_1_lreg));
  opc opc_1 (
    .sel0(opc_1_sel0), .sel1(opc_1_sel1), .lop(opc_1_lop), .ex(opc_1_ex), .excout(opc_1_excout),
    .op1out(opc_1_op1out), .op2out(opc_1_op2out), .dbusout(auxregs_1_dbusout), .op0out(opc_1_op0out),
    .op(opc_1_op), .dbus(auxregs_1_dbusout), .fall(and_4_out), .cc(control_1_cc), .eop1(control_1_eop1),
    .eop2(control_1_eop2), .clk(and_3_out));
  ROM #(.addrWidth(15)) rom_1 (.addr(addr_1_addrout[14:0]), .data(rom_1_data));
  RAM #(.addrWidth(15), .clearpin("true"), .enables("line")) ram_1 (
    .addr(addr_1_addrout[14:0]), .we(addr_1_lramout), .clk(and_3_out), .din(auxregs_1_dbusout),
    .dout(ram_1_dout), .clr(1'b0));
  alu alu_1 (
    .dout(auxregs_1_dbusout), .op(opc_1_op[2:0]), .clk(and_3_out), .ldx(control_1_ldx), .ldy(control_1_ldy),
    .ealu(control_1_ealu), .ldf(control_1_ldf), .fin(regs_1_fout), .din(auxregs_1_dbusout));
  dev dev_1 (
    .dbusout(auxregs_1_dbusout), .hltout(dev_1_hltout), .clk(and_3_out), .edev(control_1_edev),
    .ldev(control_1_ldev), .lprt(control_1_lprt), .dbusin(auxregs_1_dbusout));  // open: powout, errout
  assign auxregs_1_dbusout = addr_1_erom ? rom_1_data : 8'bz;  // Controlled_Buffer controlled_buffer_1
  assign auxregs_1_dbusout = addr_1_eramout ? ram_1_dout : 8'bz;  // Controlled_Buffer controlled_buffer_2
  Keyboard keyboard_1 ();  // open: clk, re, clr, avail, data

  // Notes on the sheet:
  //   contents of rom_1 (hex, n*v repeats v):
  //   0 0 1 1 2 7 b 0 9b 1 8 1 9 3 f2 1 50 6 0 6a 77 0 c7 8 87
endmodule

module screendev (
  input  clk,
  input  edev,
  input  ldev,
  input  [7:0] prt,
  input  [7:0] din,
  output [7:0] dout,
  output [5:0] sx,
  output [5:0] sy,
  output sv,
  output se
);

  wire and_1_out, and_2_out, and_3_out, and_4_out, and_5_out, and_6_out, and_7_out, and_8_out, and_9_out,
       and_10_out, and_11_out, and_12_out, and_13_out, clock_1_out, comparator_1_eq, comparator_2_eq,
       comparator_3_eq, comparator_4_eq, comparator_5_eq, counter_1_carry, counter_2_carry, counter_3_carry,
       d_ff_1_q, d_ff_2_q, d_ff_2_qn, not_1_out, not_2_out, not_3_out, not_4_out, or_1_out, or_2_out;
  wire [0:0] d_ff_3_q;
  wire [8:0] counter_2_q;

  Clock clock_1 (.out(clock_1_out));
  Comparator comparator_1 (.a(prt), .b(8'h2), .eq(comparator_1_eq));  // open: gt, lt
  Comparator comparator_2 (.a(din), .b(8'h1), .eq(comparator_2_eq));  // open: gt, lt
  Comparator comparator_3 (.a(din), .b(8'h2), .eq(comparator_3_eq));  // open: gt, lt
  Comparator comparator_4 (.a(din), .b(8'h3), .eq(comparator_4_eq));  // open: gt, lt
  Comparator comparator_5 (.a(din), .b(8'h4), .eq(comparator_5_eq));  // open: gt, lt
  not not_1 (not_1_out, d_ff_1_q);
  and and_1 (and_1_out, ldev, comparator_1_eq);
  and and_2 (and_2_out, and_1_out, not_1_out, comparator_2_eq);
  and and_3 (and_3_out, and_2_out, and_8_out);
  and and_4 (and_4_out, and_1_out, not_1_out, comparator_3_eq);
  and and_5 (and_5_out, and_4_out, and_8_out);
  and and_6 (and_6_out, and_1_out, not_1_out, comparator_4_eq);
  and and_7 (and_7_out, and_1_out, not_1_out, comparator_5_eq);
  not not_2 (not_2_out, clock_1_out);
  not not_3 (not_3_out, clock_1_out);
  not not_4 (not_4_out, not_2_out);
  and and_8 (and_8_out, not_3_out, not_4_out);
  D_Flip_Flop d_ff_1 (.D(and_2_out), .clk(and_3_out), .Q(d_ff_1_q), .reset(counter_2_carry));  // open: Qn, preset
  D_Flip_Flop d_ff_2 (
    .D(and_4_out), .clk(and_5_out), .Q(d_ff_2_q), .Qn(d_ff_2_qn), .reset(counter_2_carry));  // open: preset
  and and_9 (and_9_out, d_ff_1_q, and_1_out);
  // RGB_Video #(.cursor("No Cursor"), .height(64), .scale(6), .width(64)) rgb_video_1: pin names not known
  or or_1 (or_1_out, and_9_out, counter_1_carry);
  Counter #(.max('h7), .width(3)) counter_1 (
    .count(d_ff_2_q), .carry(counter_1_carry), .up(1'b1), .clk(clock_1_out), .clr(and_10_out));  // open: load, D, Q
  and and_10 (and_10_out, counter_1_carry, and_8_out);
  Counter #(.max('h1ff), .width(9)) counter_2 (
    .count(or_1_out), .Q(counter_2_q), .carry(counter_2_carry), .up(1'b1), .clk(and_8_out),
    .clr(counter_2_carry));  // open: load, D
  D_Flip_Flop d_ff_3 (.D(and_11_out), .clk(and_12_out), .Q(d_ff_3_q[0]));  // open: Qn, preset, reset
  and and_11 (and_11_out, d_ff_2_qn, and_7_out);
  and and_12 (and_12_out, and_7_out, clock_1_out);
  RAM #(.addrWidth(9), .clearpin("true"), .enables("line")) ram_1 (
    .addr(counter_2_q), .we(and_9_out), .clk(clock_1_out), .din(din), .clr(and_6_out));  // open: dout
  Counter #(.max('h3f), .width(6)) counter_3 (
    .count(d_ff_2_q), .Q(sx), .carry(counter_3_carry), .up(1'b1), .clk(and_8_out), .clr(or_2_out));  // open: load, D
  or or_2 (or_2_out, and_13_out, counter_2_carry);
  Counter #(.max('h3f), .width(6)) counter_4 (
    .count(counter_3_carry), .Q(sy), .up(1'b1), .clk(and_8_out), .clr(counter_2_carry));  // open: load, D, carry
  assign dout = edev ? {{7{1'b0}}, d_ff_3_q[0]} : 8'bz;  // Controlled_Buffer controlled_buffer_1
  and and_13 (and_13_out, counter_3_carry, and_8_out);
endmodule
